# Fritzing sketch fritzing-sketck (saved by Fritzing 0.9.6b)

parts:
  Mod1 = ESP32 - CAM
  HC-SR04_Sensor_1 = HC-SR04 Ultrasonic Distance Sensor

nets:
  GND: Mod1.GND, HC-SR04_Sensor_1.GND

custom parts:
  ESP32 - CAM: The ESP32-CAM has a very competitive small-size camera module that can operate independently as a minimum system with a footprint of only 27*40.5*4.5mm and a deep sleep current of up to 6mA.
